// Logisim project Datapath com controle manual.circ as structural Verilog: 11 circuits, main circuit ALU control
module ALU_control (
  input  [3:0] OPERATION,
  output [3:0] OPERATION_2
);


  assign OPERATION_2 = OPERATION;
endmodule

module ControleManual (
  input  [8:0] in_1,
  output RegDst,
  output Branch,
  output LeMem,
  output MemparaReg,
  output EscreveMem,
  output OrigALU,
  output EscreveReg,
  output [1:0] OpALU
);


  assign Branch = in_1[7];
  assign EscreveMem = in_1[2];
  assign EscreveReg = in_1[0];
  assign LeMem = in_1[6];
  assign MemparaReg = in_1[5];
  assign OpALU = in_1[4:3];
  assign OrigALU = in_1[1];
  assign RegDst = in_1[8];
endmodule

module Datapath_com_controle_manual (
  input  _1000ffff,
  input  in_2,
  input  in_3,
  input  in_4,
  input  in_5,
  input  in_6,
  input  in_7,
  input  beq___X10X01000,
  input  in_9,
  input  RESET,
  input  [3:0] OPERATION,
  input  in_12,
  input  in_13,
  output [5:0] OPCODE,
  output [3:0] out_15,
  output [1:0] OP,
  output [5:0] FUNCT
);

  wire alu_1_zero, and_1_out, CLOCK_out, controlemanual_1_branch, controlemanual_1_escrevemem,
       controlemanual_1_escrevereg, controlemanual_1_lemem, controlemanual_1_memparareg,
       controlemanual_1_origalu, controlemanual_1_regdst, not_1_out;
  wire [4:0] instructiondecode_1_rd, instructiondecode_1_rs, instructiondecode_1_rt, multiplexer_1_out;
  wire [7:0] wordaddress_1_wordaddress, wordaddress_2_wordaddress;
  wire [15:0] instructiondecode_1_immediate;
  wire [31:0] adder_1_out, alu_1_result, BRANCH_branchaddress, mips_ram_1_p7, mips_ram_2_p8,
       multiplexer_2_out, multiplexer_3_out, register_1_q, registerfile_1_p1, registerfile_1_p7,
       registerfile_1_p8, signextend_1_out_2;

  Clock CLOCK (.out(CLOCK_out));
  WordAddress wordaddress_1 (.ByteAddress(register_1_q), .WordAddress(wordaddress_1_wordaddress));  // open: Unaligned
  Register #(.width(32)) register_1 (
    .D(multiplexer_3_out), .Q(register_1_q), .clk(CLOCK_out), .clr(RESET));  // open: en
  not not_1 (not_1_out, CLOCK_out);
  InstructionDecode instructiondecode_1 (
    .Instruction(mips_ram_1_p7), .op(OPCODE), .rs(instructiondecode_1_rs), .rt(instructiondecode_1_rt),
    .rd(instructiondecode_1_rd), .funct(FUNCT), .immediate(instructiondecode_1_immediate));  // open: shamt, address
  // MIPS_RAM mips_ram_1: pin names not known; wires that end beside it: wordaddress_1_wordaddress, 1'b0, 4'b1111, 1'b0, 1'b1, in_12, mips_ram_1_p7
  ControleManual controlemanual_1 (
    .in_1({_1000ffff, in_2, in_3, in_4, in_5, in_6, in_7, beq___X10X01000, in_9}),
    .RegDst(controlemanual_1_regdst), .Branch(controlemanual_1_branch), .LeMem(controlemanual_1_lemem),
    .MemparaReg(controlemanual_1_memparareg), .EscreveMem(controlemanual_1_escrevemem),
    .OrigALU(controlemanual_1_origalu), .EscreveReg(controlemanual_1_escrevereg), .OpALU(OP));
  Multiplexer #(.width(5), .enable("false")) multiplexer_1 (
    .in0(instructiondecode_1_rt), .in1(instructiondecode_1_rd), .out(multiplexer_1_out),
    .sel(controlemanual_1_regdst));
  Adder #(.width(32)) adder_1 (.a(32'h4), .b(register_1_q), .out(adder_1_out));  // open: cin, cout
  SignExtend signextend_1 (.in_1(instructiondecode_1_immediate), .out_2(signextend_1_out_2));
  // RegisterFile registerfile_1: pin names not known; wires that end beside it: registerfile_1_p1, not_1_out, controlemanual_1_escrevereg, multiplexer_1_out, instructiondecode_1_rs, instructiondecode_1_rt, registerfile_1_p7, registerfile_1_p8
  Multiplexer #(.width(32), .enable("false")) multiplexer_2 (
    .in0(registerfile_1_p8), .in1(signextend_1_out_2), .out(multiplexer_2_out), .sel(controlemanual_1_origalu));
  BranchAd BRANCH (.PC_4(adder_1_out), .Address(signextend_1_out_2), .BranchAddress(BRANCH_branchaddress));
  ALU_control alu_control_1 (.OPERATION(OPERATION), .OPERATION_2(out_15));
  WordAddress wordaddress_2 (.ByteAddress(alu_1_result), .WordAddress(wordaddress_2_wordaddress));  // open: Unaligned
  ALU alu_1 (
    .A(registerfile_1_p7), .B(multiplexer_2_out), .Operation(out_15), .Zero(alu_1_zero), .Result(alu_1_result));  // open: Overflow
  // MIPS_RAM mips_ram_2: pin names not known; wires that end beside it: wordaddress_2_wordaddress, registerfile_1_p8, controlemanual_1_escrevemem, 4'b1111, not_1_out, controlemanual_1_lemem, in_13, mips_ram_2_p8
  Multiplexer #(.width(32), .enable("false")) multiplexer_3 (
    .in0(adder_1_out), .in1(BRANCH_branchaddress), .out(multiplexer_3_out), .sel(and_1_out));
  and and_1 (and_1_out, controlemanual_1_branch, alu_1_zero);
  Multiplexer #(.width(32), .enable("false")) multiplexer_4 (
    .in0(alu_1_result), .in1(mips_ram_2_p8), .out(registerfile_1_p1), .sel(controlemanual_1_memparareg));

  // Notes on the sheet:
  //   Opcode
  //   8c0a0000
  //   8c0b0004
  //   014b4820
  //   ac090008
  //   Instruções
  //   main:  lw $t2, 0($zero) 
  //   lw $t3, 4($zero)
  //   add $t1, $t2, $t3
  //   sw $t1, 8($zero)
  //   exit:  beq $zero, $zero, exit
  //   Controle
  //   lw    001100011
  //   lw    001100011
  //   R     100010001
  //   sw    X00X00110
  //   Controle ALU
  //   0010 add
  //   0010 add
  //   0010 add
  //   0010 add
  //   0110 sub
endmodule

module BranchAd (
  input  [31:0] PC_4,
  input  [31:0] Address,
  output [31:0] BranchAddress
);

  Adder #(.width(32)) adder_1 (.a(PC_4), .b({Address[29:0], 2'b00}), .out(BranchAddress));  // open: cin, cout
endmodule

module ALU (
  input  [31:0] A,
  input  [31:0] B,
  input  [3:0] Operation,
  output Zero,
  output [31:0] Result,
  output Overflow
);

  wire getsign_1_sign, getsign_2_sign, getsign_3_sign, xor_1_out;
  wire [31:0] adder_1_out, and_1_out, getsign_1_out_2, getsign_2_out_2, getsign_3_out_2, multiplexer_1_out,
       multiplexer_2_out, not_1_out, not_2_out, or_1_out, setlsb_1_out_3;

  assign not_1_out = ~A;  // NOT_Gate not_1, 32 bits wide
  assign not_2_out = ~B;  // NOT_Gate not_2, 32 bits wide
  Multiplexer #(.width(32), .enable("false")) multiplexer_1 (
    .in0(A), .in1(not_1_out), .out(multiplexer_1_out), .sel(Operation[3]));
  Multiplexer #(.width(32), .enable("false")) multiplexer_2 (
    .in0(B), .in1(not_2_out), .out(multiplexer_2_out), .sel(Operation[2]));
  GetSign getsign_1 (.in_1(multiplexer_1_out), .Sign(getsign_1_sign), .out_2(getsign_1_out_2));
  GetSign getsign_2 (.in_1(multiplexer_2_out), .Sign(getsign_2_sign), .out_2(getsign_2_out_2));
  Overflow overflow_1 (
    .A(getsign_1_sign), .B(getsign_2_sign), .Result(getsign_3_sign), .Operation(Operation[1:0]),
    .Overflow(Overflow));
  assign and_1_out = getsign_1_out_2 & getsign_2_out_2;  // AND_Gate and_1, 32 bits wide
  assign or_1_out = getsign_1_out_2 | getsign_2_out_2;  // OR_Gate or_1, 32 bits wide
  GetSign getsign_3 (.in_1(adder_1_out), .Sign(getsign_3_sign), .out_2(getsign_3_out_2));
  Adder #(.width(32)) adder_1 (
    .a(getsign_1_out_2), .b(getsign_2_out_2), .out(adder_1_out), .cin(Operation[2]));  // open: cout
  xor xor_1 (xor_1_out, getsign_3_sign, Overflow);
  SetLSB setlsb_1 (.in_2({32{1'b0}}), .LSB(xor_1_out), .out_3(setlsb_1_out_3));
  Multiplexer #(.select(2), .width(32), .enable("false")) multiplexer_3 (
    .in0(and_1_out), .in1(or_1_out), .in2(getsign_3_out_2), .in3(setlsb_1_out_3), .out(Result),
    .sel(Operation[1:0]));
  Zero zero_1 (.in_1(Result), .out_2(Zero));

  // Notes on the sheet:
  //   +/-
  //   +/-
  //   +/-
  //   LSB
  //   0?
endmodule

module GetSign (
  input  [31:0] in_1,
  output [31:0] out_2,
  output Sign
);


  assign out_2 = in_1;
  assign Sign = in_1[31];
endmodule

module Zero (
  input  [31:0] in_1,
  output out_2
);

  wire or_1_out, or_2_out, or_3_out, or_4_out;

  or or_1 (or_1_out, in_1[0], in_1[1], in_1[2], in_1[3], in_1[4], in_1[5], in_1[6]);
  or or_2 (or_2_out, in_1[7], in_1[8], in_1[9], in_1[10], in_1[11], in_1[12], in_1[13], in_1[14], in_1[15]);
  or or_3 (or_3_out, in_1[16], in_1[17], in_1[18], in_1[19], in_1[20], in_1[21], in_1[22], in_1[23], in_1[24]);
  or or_4 (or_4_out, in_1[25], in_1[26], in_1[27], in_1[28], in_1[29], in_1[30], in_1[31]);
  nor nor_1 (out_2, or_1_out, or_2_out, or_3_out, or_4_out);
endmodule

module SetLSB (
  input  LSB,
  input  [31:0] in_2,
  output [31:0] out_3
);


  assign out_3 = {in_2[31:1], LSB};
endmodule

module Overflow (
  input  Result,
  input  A,
  input  B,
  input  [1:0] Operation,
  output Overflow
);

  wire and_1_out, and_2_out, not_1_out, not_2_out, not_3_out, not_4_out, or_1_out;

  not not_1 (not_1_out, Result);
  not not_2 (not_2_out, A);
  not not_3 (not_3_out, B);
  not not_4 (not_4_out, Operation[0]);
  and and_1 (and_1_out, not_1_out, A, B);
  and and_2 (and_2_out, Result, not_2_out, not_3_out);
  or or_1 (or_1_out, and_1_out, and_2_out);
  and and_3 (Overflow, or_1_out, Operation[1], not_4_out);
endmodule

module InstructionDecode (
  input  [31:0] Instruction,
  output [5:0] op,
  output [4:0] rs,
  output [4:0] rt,
  output [4:0] rd,
  output [4:0] shamt,
  output [5:0] funct,
  output [15:0] immediate,
  output [25:0] address
);


  assign address = Instruction[25:0];
  assign funct = Instruction[5:0];
  assign immediate = Instruction[15:0];
  assign op = Instruction[31:26];
  assign rd = Instruction[15:11];
  assign rs = Instruction[25:21];
  assign rt = Instruction[20:16];
  assign shamt = Instruction[10:6];

  // Notes on the sheet:
  //   J-type
  //   I-type
  //   R-type
endmodule

module SignExtend (
  input  [15:0] in_1,
  output [31:0] out_2
);


  assign out_2 = {{17{in_1[15]}}, in_1[14:0]};
endmodule
