// Logisim project datapath.circ as structural Verilog: 3 circuits, main circuit Datapath
module Datapath (
  input  RESET,
  input  in_2,
  input  in_3,
  output [1:0] out_4,
  output [5:0] out_5,
  output [3:0] out_6
);

  wire alu_1_zero, and_1_out, CLOCK_out, control_1_branch, control_1_escrevemem, control_1_escrevereg,
       control_1_lemem, control_1_memparareg, control_1_origalu, control_1_regdst, not_1_out;
  wire [4:0] instruction_decode_1_rd, instruction_decode_1_rs, instruction_decode_1_rt, multiplexer_1_out;
  wire [5:0] instruction_decode_1_op;
  wire [7:0] wordaddress_1_wordaddress, wordaddress_2_wordaddress;
  wire [15:0] instruction_decode_1_immediate;
  wire [31:0] adder_1_out, alu_1_result, branchaddress_1_branchaddress, mips_ram_1_p7, mips_ram_2_p8,
       multiplexer_2_out, multiplexer_3_out, register_1_q, registerfile_1_p1, registerfile_1_p7,
       registerfile_1_p8, signextend_1_out_2;

  Clock CLOCK (.out(CLOCK_out));
  WordAddress wordaddress_1 (.ByteAddress(register_1_q), .WordAddress(wordaddress_1_wordaddress));  // open: Unaligned
  Register #(.width(32)) register_1 (
    .D(multiplexer_3_out), .Q(register_1_q), .clk(CLOCK_out), .clr(RESET));  // open: en
  not not_1 (not_1_out, CLOCK_out);
  Instruction_Decode instruction_decode_1 (
    .Instruction(mips_ram_1_p7), .op(instruction_decode_1_op), .rs(instruction_decode_1_rs),
    .rt(instruction_decode_1_rt), .rd(instruction_decode_1_rd), .funct(out_5),
    .immediate(instruction_decode_1_immediate));  // open: shamt, address
  // MIPS_RAM mips_ram_1: pin names not known; wires that end beside it: wordaddress_1_wordaddress, 1'b0, 4'b1111, 1'b0, 1'b1, in_2, mips_ram_1_p7
  Control control_1 (
    .op(instruction_decode_1_op), .RegDst(control_1_regdst), .Branch(control_1_branch),
    .LeMem(control_1_lemem), .MemparaReg(control_1_memparareg), .EscreveMem(control_1_escrevemem),
    .OrigALU(control_1_origalu), .EscreveReg(control_1_escrevereg), .OpALU(out_4));
  Multiplexer #(.width(5), .enable("false")) multiplexer_1 (
    .in0(instruction_decode_1_rt), .in1(instruction_decode_1_rd), .out(multiplexer_1_out),
    .sel(control_1_regdst));
  Adder #(.width(32)) adder_1 (.a(32'h4), .b(register_1_q), .out(adder_1_out));  // open: cin, cout
  SignExtend signextend_1 (.in_1(instruction_decode_1_immediate), .out_2(signextend_1_out_2));
  // RegisterFile registerfile_1: pin names not known; wires that end beside it: registerfile_1_p1, not_1_out, control_1_escrevereg, multiplexer_1_out, instruction_decode_1_rs, instruction_decode_1_rt, registerfile_1_p7, registerfile_1_p8
  Multiplexer #(.width(32), .enable("false")) multiplexer_2 (
    .in0(registerfile_1_p8), .in1(signextend_1_out_2), .out(multiplexer_2_out), .sel(control_1_origalu));
  BranchAddress branchaddress_1 (
    .PC_4(adder_1_out), .Address(signextend_1_out_2), .BranchAddress(branchaddress_1_branchaddress));
  ALUcontrol alucontrol_1 (.OpALU(out_4), .FUNCT(out_5), .OPERATION(out_6));
  WordAddress wordaddress_2 (.ByteAddress(alu_1_result), .WordAddress(wordaddress_2_wordaddress));  // open: Unaligned
  ALU alu_1 (
    .A(registerfile_1_p7), .B(multiplexer_2_out), .Operation(out_6), .Zero(alu_1_zero), .Result(alu_1_result));  // open: Overflow
  // MIPS_RAM mips_ram_2: pin names not known; wires that end beside it: wordaddress_2_wordaddress, registerfile_1_p8, control_1_escrevemem, 4'b1111, not_1_out, control_1_lemem, in_3, mips_ram_2_p8
  Multiplexer #(.width(32), .enable("false")) multiplexer_3 (
    .in0(adder_1_out), .in1(branchaddress_1_branchaddress), .out(multiplexer_3_out), .sel(and_1_out));
  and and_1 (and_1_out, control_1_branch, alu_1_zero);
  Multiplexer #(.width(32), .enable("false")) multiplexer_4 (
    .in0(alu_1_result), .in1(mips_ram_2_p8), .out(registerfile_1_p1), .sel(control_1_memparareg));

  // Notes on the sheet:
  //   Opcode
  //   8c0a0000
  //   8c0b0004
  //   014b4820
  //   ac090008
  //   1000ffff
  //   Instruções
  //   main:  lw $t2, 0($zero) 
  //   lw $t3, 4($zero)
  //   sw $t1, 8($zero)
  //   exit:  beq $zero, $zero, exit
  //   add $t1, $t2, $t3
  //   Controle
  //   lw    001100011
  //   lw    001100011
  //   R     100010001
  //   sw    X00X00110
  //   beq   X10X01000
  //   Controle ALU
  //   0010 add
  //   0010 add
  //   0010 add
  //   0010 add
  //   0110 sub
endmodule

module Control (
  input  [5:0] op,
  output RegDst,
  output Branch,
  output LeMem,
  output MemparaReg,
  output EscreveMem,
  output OrigALU,
  output EscreveReg,
  output [1:0] OpALU
);

  wire not_1_out, not_2_out, not_3_out, not_4_out, not_5_out, not_6_out, not_7_out, not_8_out, not_9_out,
       not_10_out, not_11_out, not_12_out, not_13_out, not_14_out, not_15_out, not_16_out;

  not not_1 (not_1_out, op[0]);
  not not_2 (not_2_out, op[1]);
  not not_3 (not_3_out, op[2]);
  not not_4 (not_4_out, op[3]);
  not not_5 (not_5_out, op[4]);
  not not_6 (not_6_out, op[5]);
  not not_7 (not_7_out, op[2]);
  not not_8 (not_8_out, op[3]);
  not not_9 (not_9_out, op[4]);
  not not_10 (not_10_out, op[2]);
  not not_11 (not_11_out, op[4]);
  not not_12 (not_12_out, op[0]);
  not not_13 (not_13_out, op[1]);
  not not_14 (not_14_out, op[3]);
  not not_15 (not_15_out, op[4]);
  not not_16 (not_16_out, op[5]);
  and Tipo_R (OpALU[1], not_1_out, not_2_out, not_3_out, not_4_out, not_5_out, not_6_out);
  and lw (LeMem, op[0], op[1], not_7_out, not_8_out, not_9_out, op[5]);
  and SW (EscreveMem, op[0], op[1], not_10_out, op[3], not_11_out, op[5]);
  and beq (Branch, not_12_out, not_13_out, op[2], not_14_out, not_15_out, not_16_out);
  or or_1 (OrigALU, LeMem, EscreveMem);
  or or_2 (EscreveReg, OpALU[1], LeMem);

  assign MemparaReg = LeMem;
  assign OpALU[0] = Branch;
  assign RegDst = OpALU[1];
endmodule

module ALUcontrol (
  input  [1:0] OpALU,
  input  [5:0] FUNCT,
  output [3:0] OPERATION
);

  wire and_1_out, and_3_out, and_4_out, and_5_out, not_1_out, not_2_out, not_3_out, not_4_out, not_5_out,
       or_1_out;

  and and_1 (and_1_out, FUNCT[5], not_1_out);
  not not_1 (not_1_out, FUNCT[4]);
  not not_2 (not_2_out, OpALU[0]);
  not not_3 (not_3_out, OpALU[1]);
  not not_4 (not_4_out, OpALU[0]);
  not not_5 (not_5_out, OpALU[1]);
  and and_2 (OPERATION[3], OpALU[0], not_2_out);
  and and_3 (and_3_out, OpALU[1], FUNCT[1]);
  and and_4 (and_4_out, not_3_out, not_4_out);
  and and_5 (and_5_out, not_5_out, OpALU[0]);
  and and_6 (OPERATION[0], OpALU[1], or_1_out);
  or or_1 (or_1_out, FUNCT[3], FUNCT[0]);
  or or_2 (OPERATION[2], OpALU[0], and_3_out);
  or or_3 (OPERATION[1], and_4_out, and_1_out, FUNCT[3], FUNCT[2], and_5_out);
endmodule
