// Logisim project control.circ as structural Verilog: 3 circuits, main circuit ALUcontrol_0
module ALUcontrol_0 (
  input  ALUop_1,
  input  ALUop_0,
  input  F5,
  input  F4,
  input  F3,
  input  F2,
  input  F1,
  input  F0,
  output Operation_3,
  output Operation_2,
  output Operation_1,
  output Operation_0
);

  wire and_1_out, not_1_out, or_1_out;

  or or_1 (or_1_out, F3, F0);
  and and_1 (and_1_out, ALUop_1, F1);
  and and_2 (Operation_3, ALUop_0, not_1_out);
  not not_1 (not_1_out, ALUop_0);
  or or_2 (Operation_2, ALUop_0, and_1_out);
  or or_3 (Operation_1, ALUop_1, F3, F2);
  and and_3 (Operation_0, ALUop_1, or_1_out);
endmodule

module Control_0 (
  input  op_5,
  input  op_4,
  input  op_3,
  input  op_2,
  input  op_1,
  input  op_0,
  output RegDst,
  output Branch,
  output MemRead,
  output MemToReg,
  output MemWrite,
  output ALUsrc,
  output RegWrite
);

  wire not_1_out, not_2_out, not_3_out, not_4_out, not_5_out, not_6_out, not_7_out, not_8_out, not_9_out,
       not_10_out, not_11_out, not_12_out, not_13_out, not_14_out, not_15_out, not_16_out;

  not not_1 (not_1_out, op_5);
  not not_2 (not_2_out, op_4);
  not not_3 (not_3_out, op_3);
  and and_1 (RegDst, not_1_out, not_2_out, not_3_out, not_4_out, not_5_out, not_6_out);
  not not_4 (not_4_out, op_2);
  not not_5 (not_5_out, op_1);
  not not_6 (not_6_out, op_0);
  not not_7 (not_7_out, op_4);
  not not_8 (not_8_out, op_3);
  and and_2 (MemRead, op_5, not_7_out, not_8_out, not_9_out, op_1, op_0);
  not not_9 (not_9_out, op_2);
  not not_10 (not_10_out, op_4);
  and and_3 (MemWrite, op_5, not_10_out, op_3, not_11_out, op_1, op_0);
  not not_11 (not_11_out, op_2);
  not not_12 (not_12_out, op_5);
  not not_13 (not_13_out, op_4);
  not not_14 (not_14_out, op_3);
  and and_4 (Branch, not_12_out, not_13_out, not_14_out, op_2, not_15_out, not_16_out);
  not not_15 (not_15_out, op_1);
  not not_16 (not_16_out, op_0);
  or or_1 (ALUsrc, MemRead, MemWrite);
  or or_2 (RegWrite, RegDst, MemRead);

  assign MemToReg = MemRead;
endmodule

module Control_1 (
  input  op_5,
  input  op_4,
  input  op_3,
  input  op_2,
  input  op_1,
  input  op_0,
  output ALUop_1,
  output ALUop_0
);

  wire not_1_out, not_2_out, not_3_out, not_4_out, not_5_out, not_6_out, not_7_out, not_8_out, not_9_out,
       not_10_out, not_11_out;

  not not_1 (not_1_out, op_5);
  not not_2 (not_2_out, op_4);
  not not_3 (not_3_out, op_3);
  not not_4 (not_4_out, op_2);
  not not_5 (not_5_out, op_1);
  not not_6 (not_6_out, op_0);
  not not_7 (not_7_out, op_5);
  not not_8 (not_8_out, op_4);
  not not_9 (not_9_out, op_3);
  not not_10 (not_10_out, op_1);
  not not_11 (not_11_out, op_0);
  and and_1 (ALUop_1, not_1_out, not_2_out, not_3_out, not_4_out, not_5_out, not_6_out);
  and and_2 (ALUop_0, not_7_out, not_8_out, not_9_out, op_2, not_10_out, not_11_out);
endmodule
