// Logisim project datapath.circ as structural Verilog: 3 circuits, main circuit Datapath
module Datapath (
  input  RESET,
  input  in_2,
  input  in_3,
  output [1:0] OP_ALU,
  output [5:0] FUNCT,
  output [3:0] CONTROL_CODE
);

  wire alu_1_zero, and_1_out, CLOCK_out, control_1_branch, control_1_escrevemem, control_1_escrevereg,
       control_1_jump, control_1_lemem, control_1_memparareg, control_1_origalu, control_1_regdst, not_1_out;
  wire [4:0] instruction_decode_1_rd, instruction_decode_1_rs, instruction_decode_1_rt, multiplexer_1_out;
  wire [5:0] instruction_decode_1_op;
  wire [7:0] wordaddress_1_wordaddress, wordaddress_2_wordaddress;
  wire [15:0] instruction_decode_1_immediate;
  wire [25:0] instruction_decode_1_address;
  wire [31:0] adder_1_out, alu_1_result, BRANCH_branchaddress, JUMP_jumpaddress, mips_ram_1_p7,
       mips_ram_2_p8, multiplexer_2_out, multiplexer_3_out, multiplexer_4_out, register_1_q,
       registerfile_1_p1, registerfile_1_p7, registerfile_1_p8, signextend_1_out_2;

  Clock CLOCK (.out(CLOCK_out));
  WordAddress wordaddress_1 (.ByteAddress(register_1_q), .WordAddress(wordaddress_1_wordaddress));  // open: Unaligned
  Register #(.width(32)) register_1 (
    .D(multiplexer_3_out), .Q(register_1_q), .clk(CLOCK_out), .clr(RESET));  // open: en
  not not_1 (not_1_out, CLOCK_out);
  Instruction_Decode instruction_decode_1 (
    .Instruction(mips_ram_1_p7), .op(instruction_decode_1_op), .rs(instruction_decode_1_rs),
    .rt(instruction_decode_1_rt), .rd(instruction_decode_1_rd), .funct(FUNCT),
    .immediate(instruction_decode_1_immediate), .address(instruction_decode_1_address));  // open: shamt
  // MIPS_RAM mips_ram_1: pin names not known; wires that end beside it: wordaddress_1_wordaddress, 1'b0, 4'b1111, 1'b0, 1'b1, in_2, mips_ram_1_p7
  Control control_1 (
    .op(instruction_decode_1_op), .RegDst(control_1_regdst), .Branch(control_1_branch),
    .LeMem(control_1_lemem), .MemparaReg(control_1_memparareg), .EscreveMem(control_1_escrevemem),
    .OrigALU(control_1_origalu), .EscreveReg(control_1_escrevereg), .OpALU(OP_ALU), .Jump(control_1_jump));
  Multiplexer #(.width(5), .enable("false")) multiplexer_1 (
    .in0(instruction_decode_1_rt), .in1(instruction_decode_1_rd), .out(multiplexer_1_out),
    .sel(control_1_regdst));
  Adder #(.width(32)) adder_1 (.a(32'h4), .b(register_1_q), .out(adder_1_out));  // open: cin, cout
  SignExtend signextend_1 (.in_1(instruction_decode_1_immediate), .out_2(signextend_1_out_2));
  // RegisterFile registerfile_1: pin names not known; wires that end beside it: registerfile_1_p1, not_1_out, control_1_escrevereg, multiplexer_1_out, instruction_decode_1_rs, instruction_decode_1_rt, registerfile_1_p7, registerfile_1_p8
  JumpAddress JUMP (.Address(instruction_decode_1_address), .PC_4(adder_1_out), .JumpAddress(JUMP_jumpaddress));
  Multiplexer #(.width(32), .enable("false")) multiplexer_2 (
    .in0(registerfile_1_p8), .in1(signextend_1_out_2), .out(multiplexer_2_out), .sel(control_1_origalu));
  WordAddress wordaddress_2 (.ByteAddress(alu_1_result), .WordAddress(wordaddress_2_wordaddress));  // open: Unaligned
  BranchAddress BRANCH (.PC_4(adder_1_out), .Address(signextend_1_out_2), .BranchAddress(BRANCH_branchaddress));
  ALU alu_1 (
    .A(registerfile_1_p7), .B(multiplexer_2_out), .Operation(CONTROL_CODE), .Zero(alu_1_zero),
    .Result(alu_1_result));  // open: Overflow
  ALUcontrol alucontrol_1 (.funct(FUNCT), .ALUop(OP_ALU), .Operation(CONTROL_CODE));
  // MIPS_RAM mips_ram_2: pin names not known; wires that end beside it: wordaddress_2_wordaddress, registerfile_1_p8, control_1_escrevemem, 4'b1111, not_1_out, control_1_lemem, in_3, mips_ram_2_p8
  Multiplexer #(.width(32), .enable("false")) multiplexer_3 (
    .in0(multiplexer_4_out), .in1(JUMP_jumpaddress), .out(multiplexer_3_out), .sel(control_1_jump));
  Multiplexer #(.width(32), .enable("false")) multiplexer_4 (
    .in0(adder_1_out), .in1(BRANCH_branchaddress), .out(multiplexer_4_out), .sel(and_1_out));
  and and_1 (and_1_out, control_1_branch, alu_1_zero);
  Multiplexer #(.width(32), .enable("false")) multiplexer_5 (
    .in0(alu_1_result), .in1(mips_ram_2_p8), .out(registerfile_1_p1), .sel(control_1_memparareg));

  // Notes on the sheet:
  //   Opcode
  //   8c0a0000
  //   8c0b0004
  //   014b4820
  //   ac090008
  //   1000ffff
  //   Instruções
  //   main:  lw $t2, 0($zero) 
  //   lw $t3, 4($zero)
  //   sw $t1, 8($zero)
  //   exit:  beq $zero, $zero, exit
  //   add $t1, $t2, $t3
  //   Controle
  //   lw    001100011
  //   lw    001100011
  //   R     100010001
  //   sw    X00X00110
  //   beq   X10X01000
  //   Controle ALU
  //   0010 add
  //   0010 add
  //   0010 add
  //   0010 add
  //   0110 sub
  //   ALU - CONTROL
endmodule

// CONTROLE
module Control (
  input  [5:0] op,
  output RegDst,
  output Branch,
  output LeMem,
  output MemparaReg,
  output EscreveMem,
  output OrigALU,
  output EscreveReg,
  output [1:0] OpALU,
  output Jump
);

  wire addi_out, not_1_out, not_2_out, not_3_out, not_4_out, not_5_out, not_6_out, not_7_out, not_8_out,
       not_9_out, not_10_out, not_11_out, not_12_out, not_13_out, not_14_out, not_15_out, not_16_out,
       not_17_out, not_18_out, not_19_out, not_20_out, not_21_out, not_22_out, not_23_out, not_24_out,
       not_25_out, not_26_out;

  not not_1 (not_1_out, op[0]);
  not not_2 (not_2_out, op[1]);
  not not_3 (not_3_out, op[2]);
  not not_4 (not_4_out, op[3]);
  not not_5 (not_5_out, op[4]);
  not not_6 (not_6_out, op[5]);
  not not_7 (not_7_out, op[2]);
  not not_8 (not_8_out, op[3]);
  not not_9 (not_9_out, op[4]);
  not not_10 (not_10_out, op[2]);
  not not_11 (not_11_out, op[4]);
  not not_12 (not_12_out, op[0]);
  not not_13 (not_13_out, op[1]);
  not not_14 (not_14_out, op[3]);
  not not_15 (not_15_out, op[4]);
  not not_16 (not_16_out, op[5]);
  not not_17 (not_17_out, op[0]);
  not not_18 (not_18_out, op[2]);
  not not_19 (not_19_out, op[3]);
  not not_20 (not_20_out, op[4]);
  not not_21 (not_21_out, op[5]);
  not not_22 (not_22_out, op[0]);
  not not_23 (not_23_out, op[1]);
  not not_24 (not_24_out, op[2]);
  not not_25 (not_25_out, op[4]);
  not not_26 (not_26_out, op[5]);
  and Tipo_R (OpALU[1], not_1_out, not_2_out, not_3_out, not_4_out, not_5_out, not_6_out);
  and lw (LeMem, op[0], op[1], not_7_out, not_8_out, not_9_out, op[5]);
  and SW (EscreveMem, op[0], op[1], not_10_out, op[3], not_11_out, op[5]);
  and beq (Branch, not_12_out, not_13_out, op[2], not_14_out, not_15_out, not_16_out);
  and u_Jump (Jump, not_17_out, op[1], not_18_out, not_19_out, not_20_out, not_21_out);
  and addi (addi_out, not_22_out, not_23_out, not_24_out, op[3], not_25_out, not_26_out);
  or or_1 (OrigALU, LeMem, addi_out, EscreveMem);
  or or_2 (EscreveReg, OpALU[1], addi_out, LeMem);

  assign MemparaReg = LeMem;
  assign OpALU[0] = Branch;
  assign RegDst = OpALU[1];
endmodule

module ALUcontrol (
  input  [5:0] funct,
  input  [1:0] ALUop,
  output [3:0] Operation
);

  wire and_1_out, and_2_out, and_3_out, and_4_out, not_1_out, not_2_out, not_3_out, not_4_out, not_5_out,
       or_1_out;

  and and_1 (and_1_out, funct[5], not_1_out);
  not not_1 (not_1_out, funct[4]);
  not not_2 (not_2_out, ALUop[1]);
  and and_2 (and_2_out, not_2_out, not_3_out);
  not not_3 (not_3_out, ALUop[0]);
  not not_4 (not_4_out, ALUop[1]);
  and and_3 (and_3_out, not_4_out, ALUop[0]);
  or or_1 (or_1_out, funct[3], funct[0]);
  not not_5 (not_5_out, ALUop[0]);
  and and_4 (and_4_out, ALUop[1], funct[1]);
  or or_2 (Operation[1], and_2_out, funct[3], funct[2], and_1_out, and_3_out);
  and and_5 (Operation[0], ALUop[1], or_1_out);
  and and_6 (Operation[3], ALUop[0], not_5_out);
  or or_3 (Operation[2], ALUop[0], and_4_out);
endmodule
